// Logisim project USR.circ as structural Verilog: 1 circuit, main circuit main
module main (
  input  clear,
  input  [1:0] S1__S0,
  input  Switch,
  input  Shift_Right_y1,
  input  Shift_Left_y2,
  input  x3,
  input  x2,
  input  x1,
  input  x0,
  output Q3,
  output Q2,
  output Q1,
  output Q0
);

  wire CLK_out, multiplexer_1_out, multiplexer_2_out, multiplexer_3_out, multiplexer_4_out;

  Clock CLK (.out(CLK_out));
  LED led_1 (.in(Q3));
  D_Flip_Flop d_ff_1 (.clk(CLK_out), .D(multiplexer_1_out), .Q(Q3), .reset(clear));  // open: Qn, preset, en
  Multiplexer #(.select(2)) multiplexer_1 (
    .in0(Q3), .in1(Shift_Right_y1), .in2(Q2), .in3(x3), .out(multiplexer_1_out), .sel(S1__S0), .en(Switch));
  D_Flip_Flop d_ff_2 (.clk(CLK_out), .D(multiplexer_2_out), .Q(Q2), .reset(clear));  // open: Qn, preset, en
  Multiplexer #(.select(2)) multiplexer_2 (
    .in0(Q2), .in1(Q3), .in2(Q1), .in3(x2), .out(multiplexer_2_out), .sel(S1__S0), .en(Switch));
  LED led_2 (.in(Q2));
  LED led_3 (.in(Q1));
  D_Flip_Flop d_ff_3 (.clk(CLK_out), .D(multiplexer_3_out), .Q(Q1), .reset(clear));  // open: Qn, preset, en
  Multiplexer #(.select(2)) multiplexer_3 (
    .in0(Q1), .in1(Q2), .in2(Q0), .in3(x1), .out(multiplexer_3_out), .sel(S1__S0), .en(Switch));
  D_Flip_Flop d_ff_4 (.clk(CLK_out), .D(multiplexer_4_out), .Q(Q0), .reset(clear));  // open: Qn, preset, en
  Multiplexer #(.select(2)) multiplexer_4 (
    .in0(Q0), .in1(Q1), .in2(Shift_Left_y2), .in3(x0), .out(multiplexer_4_out), .sel(S1__S0), .en(Switch));
  LED led_4 (.in(Q0));

  // Notes on the sheet:
  //   Universal shift register
  //   Batch 7
  //   Parallel outputs
  //   parallel inputs
endmodule
